# Fritzing sketch Circuit (saved by Fritzing 0.9.4)
breadboards: 1

parts:
  WeMos_D1_Mini2 = WeMos D1 Mini
  Part1 = Solid State High Level Relay Module [package=relay]
  S1 = Round Pushbutton
  J1 = Power Jack [package=power_jack_slot]
  DS1 = DS18B20 1-Wire Temperature Sensor Probe Cable
  R1 = Resistor [tolerance=±5% resistance=4.7k package="1206 [SMD]"]
  Mod1 = KY-022 Infrared Receiver Module [package="Breakout board"]
  R2 = Resistor [tolerance=±5% resistance=470 package="1206 [SMD]"]
  U1 = WS2812 RGB LED strip
  LED1 = smd LED [color="Green (560nm)" package="1206 [SMD]"]
  LED2 = smd LED [color="Red (660nm)" package="1206 [SMD]"]

nets:
  3V3: WeMos_D1_Mini2.3V3, DS1.VDD, R1.Pin_1, Mod1.Vin
  5V: WeMos_D1_Mini2.5V, Part1.DC+, S1.leg1, U1.VCC
  N1: WeMos_D1_Mini2.D2, DS1.DQ, R1.Pin_0
  N2: WeMos_D1_Mini2.D3, LED2.anode
  N3: WeMos_D1_Mini2.D4, LED1.anode
  N4: WeMos_D1_Mini2.D5, R2.Pin_1
  N5: WeMos_D1_Mini2.D7, Mod1.S
  N6: WeMos_D1_Mini2.D8, Part1.CH1
  GND: WeMos_D1_Mini2.G, Part1.DC-, DS1.GND, Mod1.-, U1.GND, LED1.cathode, LED2.cathode
  N7: Part1.A1, J1.PWR
  N8: R2.Pin_0, U1.DIN

notes:
  12V Power Adapter
  WiFi and Power LEDs
  LED Strip
  Polyimide Element
  DC Relay
  Temperature Sensor
  IR Sensor
  On/OFF

custom parts:
  Solid State High Level Relay Module: 5V Omron solid state relay 240V 2A output with resistance fuse.
  KY-022 Infrared Receiver Module: KY-022 IR receiver module, reacts to 38kHz infrared light.
  WS2812 RGB LED strip: WS2812 strip
